// Logisim project input.circ as structural Verilog: 3 circuits, main circuit main
module main (
  input  [2:0] in_1,
  output out_2
);

  wire Runway_Status_runway_a_status, Runway_Status_runway_b_status;
  wire [2:1] d_ff_2_q;
  wire [3:0] Runway_Picker_o4_o3_o2_o1;

  runway_picker Runway_Picker (.D1_D2_A_B_En({in_1[2:1], d_ff_2_q, in_1[0]}), .O4_O3_O2_O1(Runway_Picker_o4_o3_o2_o1));
  D_Flip_Flop d_ff_1 (
    .clk(in_1[0]), .D(Runway_Status_runway_a_status), .Q(d_ff_2_q[2]));  // open: Qn, preset, en, reset
  D_Flip_Flop d_ff_2 (
    .clk(in_1[0]), .D(Runway_Status_runway_b_status), .Q(d_ff_2_q[1]));  // open: Qn, preset, en, reset
  runway_status Runway_Status (
    .Runway_B_Status(Runway_Status_runway_b_status), .Runway_A_Status(Runway_Status_runway_a_status),
    .Wait_signal(out_2), .I4__I3_I2_I1_En({Runway_Picker_o4_o3_o2_o1, in_1[0]}));
endmodule

module runway_status (
  input  [4:0] I4__I3_I2_I1_En,
  output Runway_B_Status,
  output Runway_A_Status,
  output Wait_signal
);

  wire clock_1_out, clock_2_out, counter_1_carry, counter_2_carry, demultiplexer_1_out10,
       demultiplexer_1_out11, not_1_out, not_2_out, not_3_out, not_4_out, s_r_ff_1_q, s_r_ff_2_q;

  Demultiplexer #(.select(4)) demultiplexer_1 (
    .out10(demultiplexer_1_out10), .out11(demultiplexer_1_out11), .out13(Wait_signal),
    .in(I4__I3_I2_I1_En[0]), .sel(I4__I3_I2_I1_En[4:1]));  // open: out0, out1, out2, out3, out4, out5, out6, out7, out8, out9, out12, out14, out15, en
  Clock clock_1 (.out(clock_1_out));
  and and_1 (Runway_A_Status, not_1_out, s_r_ff_1_q);
  not not_1 (not_1_out, counter_1_carry);
  S_R_Flip_Flop s_r_ff_1 (
    .S(demultiplexer_1_out10), .clk(clock_1_out), .R(1'b0), .Q(s_r_ff_1_q), .reset(counter_1_carry));  // open: Qn, preset, en
  Counter #(.width(4), .max('hd), .ongoal("stay")) counter_1 (
    .carry(counter_1_carry), .clk(clock_1_out), .clr(not_2_out));  // open: load, D, count, Q
  not not_2 (not_2_out, s_r_ff_1_q);
  Clock clock_2 (.out(clock_2_out));
  and and_2 (Runway_B_Status, not_4_out, s_r_ff_2_q);
  S_R_Flip_Flop s_r_ff_2 (
    .S(demultiplexer_1_out11), .clk(clock_2_out), .R(1'b0), .Q(s_r_ff_2_q), .reset(counter_2_carry));  // open: Qn, preset, en
  Counter #(.width(4), .max('hd), .ongoal("stay")) counter_2 (
    .carry(counter_2_carry), .clk(clock_2_out), .clr(not_3_out));  // open: load, D, count, Q
  not not_3 (not_3_out, s_r_ff_2_q);
  not not_4 (not_4_out, counter_2_carry);
endmodule

module runway_picker (
  input  [4:0] D1_D2_A_B_En,
  output [3:0] O4_O3_O2_O1
);

  wire and_1_out, and_2_out, not_1_out, not_2_out, not_3_out, or_1_out;

  and and_1 (and_1_out, D1_D2_A_B_En[1], D1_D2_A_B_En[2]);
  not not_1 (not_1_out, D1_D2_A_B_En[1]);
  not not_2 (not_2_out, D1_D2_A_B_En[3]);
  and and_2 (and_2_out, not_1_out, not_2_out);
  not not_3 (not_3_out, and_1_out);
  or or_1 (or_1_out, D1_D2_A_B_En[2], and_2_out);
  and and_3 (O4_O3_O2_O1[3], D1_D2_A_B_En[0], 1'b1);
  and and_4 (O4_O3_O2_O1[2], D1_D2_A_B_En[0], and_1_out);
  and and_5 (O4_O3_O2_O1[1], D1_D2_A_B_En[0], not_3_out);
  and and_6 (O4_O3_O2_O1[0], D1_D2_A_B_En[0], or_1_out);

  // Notes on the sheet:
  //   Runway Picker
  //   O4 = 1
  //   O3 = A.B
  //   O2 = (A.B)'
  //   O1 = A + B'.D2'
endmodule
