// Logisim project runway_picker.circ as structural Verilog: 1 circuit, main circuit main
module main (
  input  Direction_1,
  input  Direction_2,
  input  Runway_A_status,
  input  Runway_B_status,
  output out_5,
  output out_6
);

  and and_1 (out_6, Runway_A_status, Runway_B_status);
endmodule
